// Logisim project lab1.1.circ as structural Verilog: 1 circuit, main circuit main
// Truth
module main (
  input  X,
  input  Y,
  input  Z,
  output F
);

  wire and_1_out, and_2_out, and_3_out, or_1_out;

  and and_1 (and_1_out, X, Y);
  or or_1 (or_1_out, and_1_out, and_2_out);
  and and_2 (and_2_out, X, Z);
  and and_3 (and_3_out, Z, Y);
  or or_2 (F, or_1_out, and_3_out);

  // Notes on the sheet:
  //   输入引脚
  //   请勿增加、删除引脚，用隧道标签构建电路，
  //   3输入多数表决器电路
  //   请勿更改电路封装外观。
  //   输出引脚
endmodule
