// Logisim project lab2.2.circ as structural Verilog: 1 circuit, main circuit main
module main (
  input  I0,
  input  I1,
  input  I2,
  input  I4,
  input  I5,
  input  I3,
  input  I6,
  input  I7,
  output O0,
  output O1,
  output O2
);

  wire and_1_out, and_2_out, and_3_out, and_4_out, and_5_out, and_6_out, and_7_out, and_8_out, and_9_out,
       and_10_out, and_11_out, and_12_out, and_13_out, and_14_out, and_15_out, and_16_out, and_17_out,
       and_18_out, and_19_out, and_20_out, and_21_out, and_22_out, and_23_out, and_24_out, and_25_out,
       and_26_out, and_27_out, and_28_out, not_1_out, not_2_out, not_3_out, not_4_out, not_5_out, not_6_out,
       not_7_out, or_1_out, or_3_out, or_4_out, or_5_out, or_7_out, or_9_out, or_10_out, or_11_out;
  wire [3:0] undriven;

  not not_1 (not_1_out, I0);
  not not_2 (not_2_out, I1);
  not not_3 (not_3_out, I2);
  not not_4 (not_4_out, I3);
  not not_5 (not_5_out, I4);
  not not_6 (not_6_out, I5);
  not not_7 (not_7_out, I6);
  // NOT_Gate not_8 has open pins: in=I7, out=open
  and and_1 (and_1_out, not_1_out, I1);
  and and_2 (and_2_out, not_1_out, not_2_out);
  and and_3 (and_3_out, not_1_out, not_2_out);
  and and_4 (and_4_out, not_3_out, I3);
  and and_5 (and_5_out, not_1_out, not_2_out);
  and and_6 (and_6_out, not_3_out, not_4_out);
  and and_7 (and_7_out, and_2_out, I2);
  and and_8 (and_8_out, and_3_out, and_4_out);
  and and_9 (and_9_out, and_5_out, and_10_out);
  and and_10 (and_10_out, and_6_out, I4);
  and and_11 (and_11_out, not_4_out, not_3_out);
  and and_12 (and_12_out, and_11_out, and_13_out);
  and and_13 (and_13_out, not_2_out, not_1_out);
  and and_14 (and_14_out, not_5_out, I5);
  and and_15 (and_15_out, not_4_out, not_3_out);
  and and_16 (and_16_out, and_15_out, and_17_out);
  and and_17 (and_17_out, not_2_out, not_1_out);
  and and_18 (and_18_out, not_6_out, not_5_out);
  and and_19 (and_19_out, and_18_out, I6);
  and and_20 (and_20_out, I7, not_6_out);
  and and_21 (and_21_out, and_20_out, and_22_out);
  and and_22 (and_22_out, not_1_out, not_2_out);
  and and_23 (and_23_out, not_3_out, not_4_out);
  and and_24 (and_24_out, and_23_out, and_25_out);
  and and_25 (and_25_out, not_5_out, not_7_out);
  and and_26 (and_26_out, and_12_out, and_14_out);
  and and_27 (and_27_out, and_16_out, and_19_out);
  and and_28 (and_28_out, and_21_out, and_24_out);
  or or_1 (or_1_out, and_27_out, and_9_out);
  or or_2 (O0, or_1_out, or_3_out);
  or or_3 (or_3_out, and_26_out, and_28_out);
  or or_4 (or_4_out, and_7_out, and_8_out);
  or or_5 (or_5_out, and_27_out, and_28_out);
  or or_6 (O1, or_5_out, or_4_out);
  buf or_7 (or_7_out, and_26_out);  // OR_Gate
  or or_8 (O2, or_7_out, or_10_out);
  buf or_9 (or_9_out, and_28_out);  // OR_Gate
  or or_10 (or_10_out, or_9_out, or_11_out);
  or or_11 (or_11_out, and_1_out, and_8_out);
  Hex_Digit_Display hex_digit_display_1 (.value(undriven));  // open: dp

  // Notes on the sheet:
  //   输入引脚
  //   请勿修改引脚名称、电路名称及电路封装外观
  //   提示：使用独立逻辑门实现8-3优先级编码器，禁止直接使用编码器组件。
  //   输出引脚
endmodule
