// Logisim project lab2.4.circ as structural Verilog: 3 circuits, main circuit main
module main (
  input  [6:0] Input,
  output [6:0] Output,
  output NoError
);

  wire \n3_8译码器_1_y0_l , \n3_8译码器_1_y1_l , \n3_8译码器_1_y2_l , \n3_8译码器_1_y3_l , \n3_8译码器_1_y4_l ,
       \n3_8译码器_1_y5_l , \n3_8译码器_1_y6_l , \n3_8译码器_1_y7_l , \n4位奇偶校验器_1_odd , \n4位奇偶校验器_2_odd ,
       \n4位奇偶校验器_3_odd , not_1_out, not_2_out, not_3_out, not_4_out, not_5_out, not_6_out, not_7_out;

  \_4位奇偶校验器  \u_4位奇偶校验器_1  (
    .N0(Input[0]), .N1(Input[2]), .N2(Input[4]), .N3(Input[6]), .ODD(\n4位奇偶校验器_1_odd ));  // open: EVEN
  \_4位奇偶校验器  \u_4位奇偶校验器_2  (
    .N0(Input[1]), .N1(Input[2]), .N2(Input[5]), .N3(Input[6]), .ODD(\n4位奇偶校验器_2_odd ));  // open: EVEN
  \_4位奇偶校验器  \u_4位奇偶校验器_3  (
    .N0(Input[4]), .N1(Input[3]), .N2(Input[5]), .N3(Input[6]), .ODD(\n4位奇偶校验器_3_odd ));  // open: EVEN
  \_3_8译码器  \u_3_8译码器_1  (
    .A(\n4位奇偶校验器_3_odd ), .B(\n4位奇偶校验器_2_odd ), .C(\n4位奇偶校验器_1_odd ), .Y0_L(\n3_8译码器_1_y0_l ),
    .Y1_L(\n3_8译码器_1_y1_l ), .Y2_L(\n3_8译码器_1_y2_l ), .Y3_L(\n3_8译码器_1_y3_l ), .Y4_L(\n3_8译码器_1_y4_l ),
    .Y5_L(\n3_8译码器_1_y5_l ), .Y6_L(\n3_8译码器_1_y6_l ), .Y7_L(\n3_8译码器_1_y7_l ));  // open: G1, G2A_L, G2B_L
  not not_1 (not_1_out, \n3_8译码器_1_y1_l );
  not not_2 (not_2_out, \n3_8译码器_1_y2_l );
  not not_3 (not_3_out, \n3_8译码器_1_y3_l );
  not not_4 (not_4_out, \n3_8译码器_1_y4_l );
  not not_5 (not_5_out, \n3_8译码器_1_y5_l );
  not not_6 (not_6_out, \n3_8译码器_1_y6_l );
  not not_7 (not_7_out, \n3_8译码器_1_y7_l );
  xor xor_1 (Output[0], not_1_out, Input[0]);
  xor xor_2 (Output[1], not_2_out, Input[1]);
  xor xor_3 (Output[2], not_3_out, Input[2]);
  xor xor_4 (Output[3], not_4_out, Input[3]);
  xor xor_5 (Output[4], not_5_out, Input[4]);
  xor xor_6 (Output[5], not_6_out, Input[5]);
  xor xor_7 (Output[6], not_7_out, Input[6]);
  not not_8 (NoError, \n3_8译码器_1_y0_l );
  Hex_Digit_Display hex_digit_display_1 ();  // open: value, dp

  // Notes on the sheet:
  //   输入引脚
  //   输入引脚
  //   请勿修改引脚名称、电路名称及电路封装外观
  //   提示：使用异或门、4位奇偶校验电路和74x138子电路实现7位汉明码纠错电路。
  //   输出引脚
endmodule

module \_3_8译码器  (
  input  G1,
  input  G2A_L,
  input  G2B_L,
  input  A,
  input  B,
  input  C,
  output Y0_L,
  output Y1_L,
  output Y2_L,
  output Y3_L,
  output Y4_L,
  output Y5_L,
  output Y6_L,
  output Y7_L
);

  wire not_1_out, not_2_out, not_3_out;

  not not_1 (not_1_out, A);
  not not_2 (not_2_out, B);
  not not_3 (not_3_out, C);
  nand nand_1 (Y0_L, not_1_out, not_2_out, not_3_out);
  nand nand_2 (Y1_L, not_1_out, not_2_out, C);
  nand nand_3 (Y2_L, not_1_out, not_3_out, B);
  nand nand_4 (Y3_L, not_1_out, B, C);
  nand nand_5 (Y4_L, A, not_2_out, not_3_out);
  nand nand_6 (Y5_L, A, C, not_2_out);
  nand nand_7 (Y6_L, B, A, not_3_out);
  nand nand_8 (Y7_L, A, B, C);

  // Notes on the sheet:
  //   3-8译码器
endmodule

module \_4位奇偶校验器  (
  input  N0,
  input  N1,
  input  N2,
  input  N3,
  output EVEN,
  output ODD
);

  wire xor_1_out, xor_2_out;

  xor xor_1 (xor_1_out, N0, N1);
  xor xor_2 (xor_2_out, N2, N3);
  not not_1 (EVEN, ODD);
  xor xor_3 (ODD, xor_1_out, xor_2_out);

  // Notes on the sheet:
  //   4位奇偶校验电路
endmodule
