// Logisim project lab2.5.circ as structural Verilog: 1 circuit, main circuit main
module main (
  input  [7:0] DataIn,
  input  [2:0] shamt,
  input  L_R,
  input  A_L,
  output [7:0] DataOut
);

  wire [7:0] multiplexer_1_out, multiplexer_2_out, multiplexer_3_out, multiplexer_4_out, multiplexer_5_out;

  Multiplexer #(.select(2), .width(8), .enable("false")) multiplexer_1 (
    .in0({1'b0, DataIn[7:1]}), .in1({DataIn[6:0], 1'b0}), .in2({{2{DataIn[7]}}, DataIn[6:1]}),
    .in3({DataIn[6:0], DataIn[7]}), .out(multiplexer_1_out), .sel({A_L, L_R}));
  Multiplexer #(.width(8), .enable("false")) multiplexer_2 (
    .in0(DataIn), .in1(multiplexer_1_out), .out(multiplexer_2_out), .sel(shamt[0]));
  Multiplexer #(.width(8), .enable("false")) multiplexer_3 (
    .in0(multiplexer_2_out), .in1(multiplexer_4_out), .out({multiplexer_3_out[3:0], multiplexer_3_out[7:4]}),
    .sel(shamt[1]));
  Multiplexer #(.select(2), .width(8), .enable("false")) multiplexer_4 (
    .in0({2'b00, multiplexer_2_out[7:2]}), .in1({multiplexer_2_out[5:0], 2'b00}),
    .in2({{3{multiplexer_2_out[7]}}, multiplexer_2_out[6:2]}),
    .in3({multiplexer_2_out[5:0], multiplexer_2_out[7:6]}), .out(multiplexer_4_out), .sel({A_L, L_R}));
  Multiplexer #(.select(2), .width(8), .enable("false")) multiplexer_5 (
    .in0({4'b0000, multiplexer_3_out[3:0]}), .in1({multiplexer_3_out[7:4], 4'b0000}),
    .in2({{5{multiplexer_3_out[3]}}, multiplexer_3_out[2:0]}), .in3(multiplexer_3_out),
    .out(multiplexer_5_out), .sel({A_L, L_R}));
  Multiplexer #(.width(8), .enable("false")) multiplexer_6 (
    .in0({multiplexer_3_out[3:0], multiplexer_3_out[7:4]}), .in1(multiplexer_5_out), .out(DataOut),
    .sel(shamt[2]));

  // Other names for the same wires on the sheet: Din[7:0] = DataIn; Left_Right = L_R; Arth_Logic = A_L;
  //   Dout[7:0] = DataOut

  // Notes on the sheet:
  //   L/R,A/L: 00逻辑右移，01算术右移，10逻辑左移，11：循环左移
  //   输入引脚
  //   循环左1
  //   补0左移1
  //   符号右移1
  //   补0右移1
  //   请勿修改引脚名称、电路名称及电路封装外观
  //   提示：使用多路选择器级联实现8位桶形移位器，禁止直接使用移位器组件。
  //   输出引脚
  //   循环左2
  //   补0左移2
  //   符号右移2
  //   补0右移2
  //   循环左4
  //   补0左移4
  //   符号右移4
  //   补0右移4
endmodule
