// Logisim project lab3.2.circ as structural Verilog: 1 circuit, main circuit SHRG4U
module SHRG4U (
  input  CLK,
  input  CLR_L,
  input  RIN,
  input  D3,
  input  D2,
  input  D1,
  input  D0,
  input  LIN,
  input  S1,
  input  S0,
  output Q3,
  output Q2,
  output Q1,
  output Q0,
  output [7:0] out_15
);

  wire and_1_out, and_2_out, and_3_out, and_4_out, and_5_out, and_6_out, and_7_out, and_8_out, and_9_out,
       and_10_out, and_11_out, and_12_out, and_13_out, and_14_out, and_15_out, and_16_out, and_17_out,
       and_18_out, and_19_out, and_20_out, not_1_out, not_2_out, not_3_out, not_4_out, or_1_out, or_2_out,
       or_3_out, or_4_out, xor_1_out, xor_2_out, xor_3_out, xor_4_out, xor_5_out, xor_6_out;

  not not_1 (not_1_out, CLR_L);
  not not_2 (not_2_out, S1);
  not not_3 (not_3_out, S0);
  not not_4 (not_4_out, CLK);
  and and_1 (and_1_out, not_2_out, not_3_out);
  and and_2 (and_2_out, not_2_out, S0);
  and and_3 (and_3_out, S1, S0);
  and and_4 (and_4_out, S1, not_3_out);
  and and_5 (and_5_out, and_1_out, Q3);
  and and_6 (and_6_out, and_2_out, Q2);
  and and_7 (and_7_out, and_3_out, out_15[6]);
  and and_8 (and_8_out, and_4_out, RIN);
  and and_9 (and_9_out, and_1_out, Q2);
  and and_10 (and_10_out, and_2_out, Q1);
  and and_11 (and_11_out, and_3_out, out_15[7]);
  and and_12 (and_12_out, and_4_out, Q3);
  and and_13 (and_13_out, and_1_out, Q1);
  and and_14 (and_14_out, and_2_out, Q0);
  and and_15 (and_15_out, and_3_out, out_15[5]);
  and and_16 (and_16_out, and_4_out, Q2);
  and and_17 (and_17_out, and_1_out, Q0);
  and and_18 (and_18_out, and_2_out, LIN);
  and and_19 (and_19_out, and_3_out, out_15[4]);
  and and_20 (and_20_out, and_4_out, Q1);
  or or_1 (or_1_out, and_6_out, and_8_out, and_5_out, and_7_out);
  or or_2 (or_2_out, and_10_out, and_12_out, and_9_out, and_11_out);
  or or_3 (or_3_out, and_14_out, and_16_out, and_13_out, and_15_out);
  or or_4 (or_4_out, and_18_out, and_20_out, and_17_out, and_19_out);
  D_Flip_Flop #(.trigger("falling")) QD (.clk(not_4_out), .D(or_1_out), .Q(Q3), .reset(not_1_out));  // open: Qn, preset
  D_Flip_Flop #(.trigger("falling")) QC (.clk(not_4_out), .D(or_2_out), .Q(Q2), .reset(not_1_out));  // open: Qn, preset
  D_Flip_Flop #(.trigger("falling")) QB (.clk(not_4_out), .D(or_3_out), .Q(Q1), .reset(not_1_out));  // open: Qn, preset
  D_Flip_Flop #(.trigger("falling")) QA (.clk(not_4_out), .D(or_4_out), .Q(Q0), .reset(not_1_out));  // open: Qn, preset
  xor xor_1 (xor_1_out, Q3, Q2);
  xor xor_2 (xor_2_out, Q3, Q1);
  xor xor_3 (xor_3_out, Q3, Q0);
  xor xor_4 (xor_4_out, Q2, Q1);
  xor xor_5 (xor_5_out, Q2, Q0);
  xor xor_6 (xor_6_out, Q1, Q0);
  xor xor_7 (out_15[0], xor_2_out, xor_1_out);
  xor xor_8 (out_15[1], xor_3_out, xor_1_out);
  xor xor_9 (out_15[2], xor_1_out, xor_4_out);
  xor xor_10 (out_15[3], xor_4_out, xor_6_out);
  xor xor_11 (out_15[4], xor_3_out, xor_2_out);
  xor xor_12 (out_15[5], xor_4_out, xor_5_out);
  xor xor_13 (out_15[6], xor_6_out, xor_5_out);
  xor xor_14 (out_15[7], xor_1_out, xor_6_out);

  // Notes on the sheet:
  //   输入引脚
  //   请勿修改引脚名称、电路名称及电路封装外观
  //   提示：使用独立逻辑门实现4位异步清零移位寄存器，禁止直接使用移位寄存器组件。
  //   输出引脚
endmodule
