// Logisim project lab3.3.circ as structural Verilog: 5 circuits, main circuit main
module main (
  input  CLK,
  input  [3:0] X,
  input  [3:0] Y,
  input  Reset,
  input  in_5,
  input  in_6,
  output [7:0] Prod
);

  wire \_4位同步计数器_2_q3 , adder4b_1_cout, and_1_out, and_2_out, comparator_2_eq, comparator_2_gt, LOAD,
       not_1_out, not_2_out, not_3_out, not_4_out, not_5_out, not_6_out, not_7_out, not_8_out, or_1_out,
       STOP, xor_1_out;
  wire [3:0] \_4位同步计数器_q0 , controlled_buffer_1_out, controlled_buffer_3_out, controlled_buffer_4_out,
       register_1_q, \桶形移位器_dataout , \桶形移位器_dataout_2 ;
  wire [7:0] adder4b_1_f;

  Hex_Digit_Display hex_digit_display_1 (.value(X));  // open: dp
  not not_1 (not_1_out, adder4b_1_f[0]);
  xor xor_1 (xor_1_out, CLK, STOP);
  and and_1 (and_1_out, xor_1_out, not_2_out);
  not not_2 (not_2_out, STOP);
  // Probe on nothing
  Hex_Digit_Display hex_digit_display_2 (.value(Y));  // open: dp
  assign controlled_buffer_1_out = adder4b_1_f[0] ? X : 4'bz;  // Controlled_Buffer controlled_buffer_1
  assign controlled_buffer_1_out = not_1_out ? 4'b0000 : 4'bz;  // Controlled_Buffer controlled_buffer_2
  ADDER4b adder4b_1 (
    .X(controlled_buffer_1_out), .Y(register_1_q), .F(adder4b_1_f[7:4]), .Cout(adder4b_1_cout), .Cin(1'b0));
  Register #(.width(4), .Select("low")) register_1 (
    .D(controlled_buffer_3_out), .en(1'b1), .Q(register_1_q), .clk(and_1_out));  // open: clr
  assign controlled_buffer_3_out = not_4_out ? \桶形移位器_dataout  : 4'bz;  // Controlled_Buffer controlled_buffer_3
  BarrelSFT8b \u_桶形移位器  (
    .DataIn(adder4b_1_f), .shamt(3'b001), .DataOut({\桶形移位器_dataout , \桶形移位器_dataout_2 }), .IN(adder4b_1_cout));  // open: L_R, A_L
  Hex_Digit_Display hex_digit_display_3 (.value(Prod[7:4]));  // open: dp
  // Probe on register_1_q
  Register #(.width(4), .Select("low")) Y_2 (
    .D(controlled_buffer_4_out), .en(1'b1), .Q(adder4b_1_f[3:0]), .clk(and_1_out));  // open: clr
  assign controlled_buffer_4_out = and_2_out ? Y : 4'bz;  // Controlled_Buffer controlled_buffer_4
  Hex_Digit_Display hex_digit_display_4 (.value(Prod[3:0]));  // open: dp
  // Probe on adder4b_1_f[3:0]
  assign controlled_buffer_3_out = and_2_out ? 4'b0000 : 4'bz;  // Controlled_Buffer controlled_buffer_5
  not not_3 (not_3_out, and_2_out);
  assign controlled_buffer_4_out = not_3_out ? \桶形移位器_dataout_2  : 4'bz;  // Controlled_Buffer controlled_buffer_6
  // Probe on X
  // Probe on Y
  // Probe on Prod
  Multiplexer #(.width(8), .enable("false")) multiplexer_1 (
    .in0({register_1_q, adder4b_1_f[3:0]}), .in1({8{1'b0}}), .out(Prod), .sel(or_1_out));
  or or_1 (or_1_out, Reset, and_2_out);
  not not_4 (not_4_out, and_2_out);
  CNTR4U \_4位同步计数器  (
    .CLK(CLK), .CLR(Reset), .Q0(\_4位同步计数器_q0 [0]), .Q1(\_4位同步计数器_q0 [1]), .Q2(\_4位同步计数器_q0 [2]),
    .Q3(\_4位同步计数器_q0 [3]));  // open: LD, D0, D1, D2, D3, ENP, ENT, RCO
  not not_5 (not_5_out, \_4位同步计数器_q0 [0]);
  not not_6 (not_6_out, \_4位同步计数器_q0 [1]);
  not not_7 (not_7_out, \_4位同步计数器_q0 [3]);
  not not_8 (not_8_out, \_4位同步计数器_q0 [2]);
  and and_2 (and_2_out, not_5_out, not_7_out, not_8_out, not_6_out);
  Comparator #(.width(4)) comparator_1 (.a(\_4位同步计数器_q0 ), .b(4'b0000), .eq(LOAD));  // open: gt, lt
  Comparator #(.width(4)) comparator_2 (
    .a(\_4位同步计数器_q0 ), .b(4'b0101), .gt(comparator_2_gt), .eq(comparator_2_eq));  // open: lt
  or or_2 (STOP, comparator_2_gt, comparator_2_eq);
  CNTR4U \_4位同步计数器_2  (
    .CLK(in_5), .LD(\_4位同步计数器_2_q3 ), .CLR(1'b0), .D0(1'b1), .D1(1'b1), .D2(1'b1), .Q3(\_4位同步计数器_2_q3 ),
    .D3(1'b1), .ENP(in_6), .ENT(in_6));  // open: Q0, Q1, Q2, RCO

  // Other names for the same wires on the sheet: RST = Reset; Z[7:0] = Prod

  // Notes on the sheet:
  //   X
  //   输入引脚
  //   P
  //   =
  //   请勿修改引脚名称、电路名称及电路封装外观
  //   提示: 采用无符号数一位乘法实现4位二进制乘法器，禁止直接使用乘法器组件
  //   ×
  //   =
  //   输出引脚
endmodule

module CNTR4U (
  input  CLK,
  input  LD,
  input  CLR,
  input  D0,
  input  D1,
  input  D2,
  input  D3,
  input  ENP,
  input  ENT,
  output Q0,
  output Q1,
  output Q2,
  output Q3,
  output RCO
);

  wire and_1_out, and_2_out, and_3_out, and_4_out, and_5_out, and_6_out, and_7_out, and_8_out, and_9_out,
       and_10_out, and_11_out, and_12_out, not_1_out, not_2_out, not_3_out, not_4_out, not_5_out, not_6_out,
       not_7_out, not_8_out, not_9_out, not_10_out, or_1_out, or_2_out, or_3_out, or_4_out, xor_1_out,
       xor_2_out, xor_3_out;

  not not_1 (not_1_out, CLK);
  not not_2 (not_2_out, CLR);
  and and_1 (and_1_out, Q1, Q0);
  and and_2 (and_2_out, Q2, Q1, Q0);
  not not_3 (not_3_out, Q0);
  not not_4 (not_4_out, Q1);
  and and_3 (and_3_out, not_4_out, Q0);
  and and_4 (and_4_out, Q1, xor_1_out);
  xor xor_1 (xor_1_out, Q1, Q0);
  not not_5 (not_5_out, Q2);
  and and_5 (and_5_out, not_5_out, Q1, Q0);
  and and_6 (and_6_out, Q2, xor_2_out);
  xor xor_2 (xor_2_out, Q2, and_1_out);
  not not_6 (not_6_out, Q3);
  and and_7 (and_7_out, not_6_out, Q2, Q1, Q0);
  and and_8 (and_8_out, Q3, xor_3_out);
  xor xor_3 (xor_3_out, Q3, and_2_out);
  and and_9 (and_9_out, not_2_out, or_1_out);
  buf or_1 (or_1_out, not_3_out);  // OR_Gate
  and and_10 (and_10_out, not_2_out, or_2_out);
  or or_2 (or_2_out, and_3_out, and_4_out);
  and and_11 (and_11_out, not_2_out, or_3_out);
  or or_3 (or_3_out, and_5_out, and_6_out);
  and and_12 (and_12_out, not_2_out, or_4_out);
  or or_4 (or_4_out, and_7_out, and_8_out);
  D_Flip_Flop #(.trigger("falling")) d_ff_1 (
    .clk(not_1_out), .D(and_9_out), .Q(Q0), .reset(not_7_out));  // open: Qn, preset
  not not_7 (not_7_out, not_2_out);
  D_Flip_Flop #(.trigger("falling")) d_ff_2 (
    .clk(not_1_out), .D(and_10_out), .Q(Q1), .reset(not_8_out));  // open: Qn, preset
  not not_8 (not_8_out, not_2_out);
  D_Flip_Flop #(.trigger("falling")) d_ff_3 (
    .clk(not_1_out), .D(and_11_out), .Q(Q2), .reset(not_9_out));  // open: Qn, preset
  not not_9 (not_9_out, not_2_out);
  D_Flip_Flop #(.trigger("falling")) d_ff_4 (
    .clk(not_1_out), .D(and_12_out), .Q(Q3), .reset(not_10_out));  // open: Qn, preset
  not not_10 (not_10_out, not_2_out);

  // Notes on the sheet:
  //   输入引脚
  //   请勿修改引脚名称、电路名称及电路封装外观
  //   提示：使用独立逻辑门实现4位二进制同步计数器，禁止直接使用计数器组件。
  //   输出引脚
endmodule

module ADDER4b (
  input  [3:0] X,
  input  [3:0] Y,
  input  Cin,
  output [3:0] F,
  output Cout
);

  wire fa_1_cout, fa_2_cout, fa_3_cout;
  wire [3:0] bit_extender_1_out, xor_1_out;

  assign bit_extender_1_out = {{3{Cin}}, Cin};  // Bit_Extender bit_extender_1
  Hex_Digit_Display hex_digit_display_1 (.value(X), .dp(1'b0));
  assign xor_1_out = bit_extender_1_out ^ Y;  // XOR_Gate xor_1, 4 bits wide
  Hex_Digit_Display hex_digit_display_2 (.value(xor_1_out), .dp(1'b0));
  FA fa_1 (.A(X[0]), .B(xor_1_out[0]), .Cin(Cin), .F(F[0]), .Cout(fa_1_cout));
  Hex_Digit_Display hex_digit_display_3 (.value(F), .dp(1'b0));
  FA fa_2 (.A(X[1]), .B(xor_1_out[1]), .Cin(fa_1_cout), .F(F[1]), .Cout(fa_2_cout));
  FA fa_3 (.A(X[2]), .B(xor_1_out[2]), .Cin(fa_2_cout), .F(F[2]), .Cout(fa_3_cout));
  FA fa_4 (.A(X[3]), .B(xor_1_out[3]), .Cin(fa_3_cout), .F(F[3]), .Cout(Cout));

  // Other names for the same wires on the sheet: SUM[3:0] = F; 操作数x[3:0] = X; 操作数y[3:0] = Y

  // Notes on the sheet:
  //   输入引脚
  //   +
  //   =
  //   请勿修改引脚名称、电路名称及电路封装外观
  //   提示：使用独立逻辑门及全加器FA子电路实现4位二进制数加减法器，禁止直接使用加减法器组件。
  //   输出引脚
endmodule

module FA (
  input  A,
  input  B,
  input  Cin,
  output F,
  output Cout
);

  wire and_1_out, and_2_out, and_3_out;

  xor xor_1 (F, A, B, Cin);
  and and_1 (and_1_out, A, B);
  and and_2 (and_2_out, B, Cin);
  and and_3 (and_3_out, A, Cin);
  or or_1 (Cout, and_1_out, and_2_out, and_3_out);

  // Notes on the sheet:
  //   全加器
endmodule

module BarrelSFT8b (
  input  [7:0] DataIn,
  input  [2:0] shamt,
  input  IN,
  input  L_R,
  input  A_L,
  output [7:0] DataOut
);

  wire [7:0] multiplexer_1_out, multiplexer_2_out;

  Multiplexer #(.width(8), .enable("false")) multiplexer_1 (
    .in0(DataIn), .in1({IN, DataIn[7:1]}), .out(multiplexer_1_out), .sel(shamt[0]));
  Multiplexer #(.width(8), .enable("false")) multiplexer_2 (
    .in0(multiplexer_1_out), .in1({{2{IN}}, multiplexer_1_out[7:2]}), .out(multiplexer_2_out), .sel(shamt[1]));
  Multiplexer #(.select(2), .width(8), .enable("false")) multiplexer_3 ();  // open: in0, in1, in2, in3, out, sel
  Multiplexer #(.select(2), .width(8), .enable("false")) multiplexer_4 ();  // open: in0, in1, in2, in3, out, sel
  Multiplexer #(.select(2), .width(8), .enable("false")) multiplexer_5 ();  // open: in0, in1, in2, in3, out, sel
  Multiplexer #(.width(8), .enable("false")) multiplexer_6 (
    .in0(multiplexer_2_out), .in1({{4{IN}}, multiplexer_2_out[7:4]}), .out(DataOut), .sel(shamt[2]));

  // Other names for the same wires on the sheet: Din[7:0] = DataIn; Input = IN; Arth_Logic = A_L; Dout[7:0] = DataOut;
  //   Left_Right = L_R

  // Notes on the sheet:
  //   L/R,A/L: 00逻辑右移，01算术右移，10逻辑左移，11：循环左移
  //   输入引脚
  //   请勿修改引脚名称、电路名称及电路封装外观
  //   提示：使用多路选择器级联实现8位桶形移位器，禁止直接使用移位器组件。
  //   输出引脚
endmodule
