// Logisim project lab3.4.circ as structural Verilog: 1 circuit, main circuit main
module main (
  input  [4:0] R1_num,
  input  [4:0] R2_num,
  input  [4:0] Write_Reg_num,
  input  [31:0] Din,
  input  Write_Enable,
  input  Clock,
  output [31:0] Reg1Out,
  output [31:0] Reg2Out
);

  wire and_1_out, decoder_1_out0, decoder_1_out1, decoder_1_out2, decoder_1_out3, decoder_1_out4,
       decoder_1_out5, decoder_1_out6, decoder_1_out7, decoder_1_out8, decoder_1_out9, decoder_1_out10,
       decoder_1_out11, decoder_1_out12, decoder_1_out13, decoder_1_out14, decoder_1_out15, decoder_1_out16,
       decoder_1_out17, decoder_1_out18, decoder_1_out19, decoder_1_out20, decoder_1_out21, decoder_1_out22,
       decoder_1_out23, decoder_1_out24, decoder_1_out25, decoder_1_out26, decoder_1_out27, decoder_1_out28,
       decoder_1_out29, decoder_1_out30, decoder_1_out31, undriven, undriven_2, undriven_3, undriven_4,
       undriven_5, undriven_6, undriven_7, undriven_8, undriven_9, undriven_10, undriven_11, undriven_12,
       undriven_13, undriven_14, undriven_15, undriven_16, undriven_17, undriven_18, undriven_19,
       undriven_20, undriven_21, undriven_22, undriven_23, undriven_24, undriven_25, undriven_26,
       undriven_27, undriven_28, undriven_29, undriven_30, undriven_31, undriven_32;
  wire [31:0] _0_q, _1_q, _2_q, _3_q, _4_q, _5_q, _6_q, _7_q, _8_q, _9_q, register_1_q, register_2_q,
       register_3_q, register_4_q, register_5_q, register_6_q, register_7_q, register_8_q, register_9_q,
       register_10_q, register_11_q, register_12_q, register_13_q, register_14_q, register_15_q,
       register_16_q, register_17_q, register_18_q, register_19_q, register_20_q, register_21_q,
       register_22_q, undriven_33, undriven_34, undriven_35, undriven_36, undriven_37, undriven_38,
       undriven_39, undriven_40, undriven_41, undriven_42, undriven_43, undriven_44, undriven_45,
       undriven_46, undriven_47, undriven_48, undriven_49, undriven_50, undriven_51, undriven_52,
       undriven_53, undriven_54, undriven_55, undriven_56, undriven_57, undriven_58, undriven_59,
       undriven_60, undriven_61, undriven_62, undriven_63, undriven_64, undriven_65, undriven_66,
       undriven_67, undriven_68, undriven_69, undriven_70, undriven_71, undriven_72, undriven_73,
       undriven_74, undriven_75, undriven_76;

  Decoder #(.select(5), .enable("false")) decoder_1 (
    .out0(decoder_1_out0), .out1(decoder_1_out1), .out2(decoder_1_out2), .out3(decoder_1_out3),
    .out4(decoder_1_out4), .out5(decoder_1_out5), .out6(decoder_1_out6), .out7(decoder_1_out7),
    .out8(decoder_1_out8), .out9(decoder_1_out9), .out10(decoder_1_out10), .out11(decoder_1_out11),
    .out12(decoder_1_out12), .out13(decoder_1_out13), .out14(decoder_1_out14), .out15(decoder_1_out15),
    .out16(decoder_1_out16), .out17(decoder_1_out17), .out18(decoder_1_out18), .out19(decoder_1_out19),
    .out20(decoder_1_out20), .out21(decoder_1_out21), .out22(decoder_1_out22), .out23(decoder_1_out23),
    .out24(decoder_1_out24), .out25(decoder_1_out25), .out26(decoder_1_out26), .out27(decoder_1_out27),
    .out28(decoder_1_out28), .out29(decoder_1_out29), .out30(decoder_1_out30), .out31(decoder_1_out31),
    .sel(Write_Reg_num));
  and and_1 (and_1_out, Clock, Write_Enable);
  Register #(.width(32), .Select("low")) _0 (
    .D(Din), .en(decoder_1_out0), .Q(_0_q), .clk(and_1_out), .cs(undriven_32));  // open: clr, preset
  Register #(.width(32), .Select("low")) _1 (
    .D(Din), .en(decoder_1_out1), .Q(_1_q), .clk(and_1_out), .cs(undriven_31));  // open: clr, preset
  Register #(.width(32), .Select("low")) _2 (
    .D(Din), .en(decoder_1_out2), .Q(_2_q), .clk(and_1_out), .cs(undriven_30));  // open: clr, preset
  Register #(.width(32), .Select("low")) _3 (
    .D(Din), .en(decoder_1_out3), .Q(_3_q), .clk(and_1_out), .cs(undriven_29));  // open: clr, preset
  Register #(.width(32), .Select("low")) _4 (
    .D(Din), .en(decoder_1_out4), .Q(_4_q), .clk(and_1_out), .cs(undriven_28));  // open: clr, preset
  Register #(.width(32), .Select("low")) _5 (
    .D(Din), .en(decoder_1_out5), .Q(_5_q), .clk(and_1_out), .cs(undriven_27));  // open: clr, preset
  Register #(.width(32), .Select("low")) _6 (
    .D(Din), .en(decoder_1_out6), .Q(_6_q), .clk(and_1_out), .cs(undriven_26));  // open: clr, preset
  Register #(.width(32), .Select("low")) _7 (
    .D(Din), .en(decoder_1_out7), .Q(_7_q), .clk(and_1_out), .cs(undriven_25));  // open: clr, preset
  Register #(.width(32), .Select("low")) _8 (
    .D(Din), .en(decoder_1_out8), .Q(_8_q), .clk(and_1_out), .cs(undriven_24));  // open: clr, preset
  Register #(.width(32), .Select("low")) _9 (
    .D(Din), .en(decoder_1_out9), .Q(_9_q), .clk(and_1_out), .cs(undriven_23));  // open: clr, preset
  Register #(.width(32), .Select("low")) register_1 (
    .D(Din), .en(decoder_1_out10), .Q(register_1_q), .clk(and_1_out), .cs(undriven_22));  // open: clr, preset
  Register #(.width(32), .Select("low")) register_2 (
    .D(Din), .en(decoder_1_out11), .Q(register_2_q), .clk(and_1_out), .cs(undriven_21));  // open: clr, preset
  Register #(.width(32), .Select("low")) register_3 (
    .D(Din), .en(decoder_1_out12), .Q(register_3_q), .clk(and_1_out), .cs(undriven_20));  // open: clr, preset
  Register #(.width(32), .Select("low")) register_4 (
    .D(Din), .en(decoder_1_out13), .Q(register_4_q), .clk(and_1_out), .cs(undriven_19));  // open: clr, preset
  Register #(.width(32), .Select("low")) register_5 (
    .D(Din), .en(decoder_1_out14), .Q(register_5_q), .clk(and_1_out), .cs(undriven_18));  // open: clr, preset
  Register #(.width(32), .Select("low")) register_6 (
    .D(Din), .en(decoder_1_out15), .Q(register_6_q), .clk(and_1_out), .cs(undriven_17));  // open: clr, preset
  Register #(.width(32), .Select("low")) register_7 (
    .D(Din), .en(decoder_1_out16), .Q(register_7_q), .clk(and_1_out), .cs(undriven_16));  // open: clr, preset
  Register #(.width(32), .Select("low")) register_8 (
    .D(Din), .en(decoder_1_out17), .Q(register_8_q), .clk(and_1_out), .cs(undriven_15));  // open: clr, preset
  Register #(.width(32), .Select("low")) register_9 (
    .D(Din), .en(decoder_1_out18), .Q(register_9_q), .clk(and_1_out), .cs(undriven_14));  // open: clr, preset
  Register #(.width(32), .Select("low")) register_10 (
    .D(Din), .en(decoder_1_out19), .Q(register_10_q), .clk(and_1_out), .cs(undriven_13));  // open: clr, preset
  Register #(.width(32), .Select("low")) register_11 (
    .D(Din), .en(decoder_1_out20), .Q(register_11_q), .clk(and_1_out), .cs(undriven_12));  // open: clr, preset
  Register #(.width(32), .Select("low")) register_12 (
    .D(Din), .en(decoder_1_out21), .Q(register_12_q), .clk(and_1_out), .cs(undriven_11));  // open: clr, preset
  Register #(.width(32), .Select("low")) register_13 (
    .D(Din), .en(decoder_1_out22), .Q(register_13_q), .clk(and_1_out), .cs(undriven_10));  // open: clr, preset
  Register #(.width(32), .Select("low")) register_14 (
    .D(Din), .en(decoder_1_out23), .Q(register_14_q), .clk(and_1_out), .cs(undriven_9));  // open: clr, preset
  Register #(.width(32), .Select("low")) register_15 (
    .D(Din), .en(decoder_1_out24), .Q(register_15_q), .clk(and_1_out), .cs(undriven_8));  // open: clr, preset
  Register #(.width(32), .Select("low")) register_16 (
    .D(Din), .en(decoder_1_out25), .Q(register_16_q), .clk(and_1_out), .cs(undriven_7));  // open: clr, preset
  Register #(.width(32), .Select("low")) register_17 (
    .D(Din), .en(decoder_1_out26), .Q(register_17_q), .clk(and_1_out), .cs(undriven_6));  // open: clr, preset
  Register #(.width(32), .Select("low")) register_18 (
    .D(Din), .en(decoder_1_out27), .Q(register_18_q), .clk(and_1_out), .cs(undriven_5));  // open: clr, preset
  Register #(.width(32), .Select("low")) register_19 (
    .D(Din), .en(decoder_1_out28), .Q(register_19_q), .clk(and_1_out), .cs(undriven_4));  // open: clr, preset
  Register #(.width(32), .Select("low")) register_20 (
    .D(Din), .en(decoder_1_out29), .Q(register_20_q), .clk(and_1_out), .cs(undriven_3));  // open: clr, preset
  Register #(.width(32), .Select("low")) register_21 (
    .D(Din), .en(decoder_1_out30), .Q(register_21_q), .clk(and_1_out), .cs(undriven_2));  // open: clr, preset
  Register #(.width(32), .Select("low")) register_22 (
    .D(Din), .en(decoder_1_out31), .Q(register_22_q), .clk(and_1_out), .cs(undriven));  // open: clr, preset
  Multiplexer #(.select(5), .width(32), .enable("false")) multiplexer_1 (
    .in0(_0_q), .in1(_1_q), .in2(_2_q), .in3(_3_q), .in4(_4_q), .in5(_5_q), .in6(_6_q), .in7(_7_q),
    .in8(_8_q), .in9(_9_q), .in10(register_1_q), .in11(register_2_q), .in12(register_3_q),
    .in13(register_4_q), .in14(register_5_q), .in15(register_6_q), .in16(register_7_q), .in17(register_8_q),
    .in18(register_9_q), .in19(register_10_q), .in20(register_11_q), .in21(register_12_q),
    .in22(register_13_q), .in23(register_14_q), .in24(register_15_q), .in25(register_16_q),
    .in26(register_17_q), .in27(register_18_q), .in28(register_19_q), .in29(register_20_q),
    .in30(register_21_q), .in31(register_22_q), .out(Reg1Out), .sel(R1_num));
  Multiplexer #(.select(5), .width(32), .enable("false")) multiplexer_2 (
    .in0(_0_q), .in1(_1_q), .in2(_2_q), .in3(_3_q), .in4(_4_q), .in5(_5_q), .in6(_6_q), .in7(_7_q),
    .in8(_8_q), .in9(_9_q), .in10(register_1_q), .in11(register_2_q), .in12(register_3_q),
    .in13(register_4_q), .in14(register_5_q), .in15(register_6_q), .in16(register_7_q), .in17(register_8_q),
    .in18(register_9_q), .in19(register_10_q), .in20(register_11_q), .in21(register_12_q),
    .in22(register_13_q), .in23(register_14_q), .in24(register_15_q), .in25(register_16_q),
    .in26(register_17_q), .in27(register_18_q), .in28(register_19_q), .in29(register_20_q),
    .in30(register_21_q), .in31(register_22_q), .out(Reg2Out), .sel(R2_num));
  Multiplexer #(.select(5), .width(32), .enable("false")) multiplexer_3 (
    .in2(undriven_33), .in3(undriven_34), .in4(undriven_35), .in5(undriven_36), .in6(undriven_37),
    .in7(undriven_38), .in8(undriven_39), .in9(undriven_40), .in10(undriven_41), .in11(undriven_42),
    .in12(undriven_43), .in13(undriven_44));  // open: in0, in1, in14, in15, in16, in17, in18, in19, in20, in21, in22, in23, in24, in25, in26, in27, in28, in29, in30, in31, out, sel
  Multiplexer #(.select(5), .width(32), .enable("false")) multiplexer_4 (
    .in0(undriven_45), .in1(undriven_46), .in2(undriven_47), .in3(undriven_48), .in4(undriven_49),
    .in5(undriven_50), .in6(undriven_51), .in7(undriven_52), .in8(undriven_53), .in9(undriven_54),
    .in10(undriven_55), .in11(undriven_56), .in12(undriven_57), .in13(undriven_58), .in14(undriven_59),
    .in15(undriven_60), .in16(undriven_61), .in17(undriven_62), .in18(undriven_63), .in19(undriven_64),
    .in20(undriven_65), .in21(undriven_66), .in22(undriven_67), .in23(undriven_68), .in24(undriven_69),
    .in25(undriven_70), .in26(undriven_71), .in27(undriven_72), .in28(undriven_73), .in29(undriven_74),
    .in30(undriven_75), .in31(undriven_76));  // open: out, sel

  // Other names for the same wires on the sheet: CLK = Clock; RA[4:0] = R1_num; RB[4:0] = R2_num; RDA[31:0] = Reg1Out;
  //   RDB[31:0] = Reg2Out; RW[4:0] = Write_Reg_num; WE = Write_Enable

  // Notes on the sheet:
  //   输入引脚
  //   请勿修改引脚名称、电路名称及电路封装外观
  //   提示：使用译码器、多路选择器和32位寄存器及逻辑门实现寄存器堆，禁止直接使用存储器组件。
  //   输出引脚
endmodule
