// Logisim project lab3.5.circ as structural Verilog: 1 circuit, main circuit main
module main (
  input  CLK,
  input  LD,
  input  [3:0] HH1,
  input  [3:0] HH0,
  input  [3:0] MM1,
  input  [3:0] MM0,
  input  [3:0] SS1,
  input  [3:0] SS0,
  output [3:0] HH_H,
  output [3:0] HH_L,
  output [3:0] MM_H,
  output [3:0] MM_L,
  output [3:0] SS_H,
  output [3:0] SS_L,
  output LED_R,
  output LED_G,
  output LED_B,
  output INErr
);

  wire and_1_out, and_2_out, and_3_out, and_4_out, and_5_out, and_6_out, and_7_out, and_8_out, and_9_out,
       and_10_out, and_11_out, and_12_out, and_13_out, and_14_out, and_15_out, and_16_out, and_17_out,
       and_18_out, and_19_out, and_20_out, and_21_out, and_22_out, and_25_out, cntr4u_1_rco, cntr4u_2_rco,
       cntr4u_3_rco, cntr4u_4_p10, cntr4u_5_rco, cntr4u_6_rco, cntr4u_7_rco, comparator_1_eq,
       comparator_1_lt, comparator_2_lt, comparator_3_lt, comparator_4_lt, comparator_5_lt, comparator_6_lt,
       comparator_7_lt, comparator_8_lt, comparator_9_lt, comparator_10_lt, decoder_1_out0, decoder_1_out1,
       decoder_1_out2, decoder_1_out3, decoder_1_out4, decoder_1_out5, decoder_1_out6, decoder_1_out7,
       decoder_1_out8, decoder_1_out9, decoder_1_out10, decoder_1_out11, decoder_1_out12, decoder_1_out13,
       decoder_1_out14, decoder_1_out15, LED_EN, multiplexer_1_out, multiplexer_2_out, not_1_out, not_3_out,
       or_1_out, or_2_out, or_3_out, or_4_out, or_5_out, or_6_out, or_7_out, or_8_out, or_9_out, RGBLED_p5,
       START, STOP, xor_1_out, xor_2_out, xor_3_out, xor_4_out;
  wire [3:0] cntr4u_4_p12;

  Multiplexer #(.enable("false")) multiplexer_1 (.in0(LD), .in1(1'b0), .out(multiplexer_1_out), .sel(INErr));
  Comparator #(.width(4), .mode("unsigned")) comparator_1 (
    .a(HH1), .b(4'b0010), .eq(comparator_1_eq), .lt(comparator_1_lt));  // open: gt
  Comparator #(.width(4), .mode("unsigned")) comparator_2 (.a(HH0), .b(4'b0100), .lt(comparator_2_lt));  // open: gt, eq
  Comparator #(.width(4), .mode("unsigned")) comparator_3 (.a(MM1), .b(4'b0110), .lt(comparator_3_lt));  // open: gt, eq
  Comparator #(.width(4), .mode("unsigned")) comparator_4 (.a(SS1), .b(4'b0110), .lt(comparator_4_lt));  // open: gt, eq
  Multiplexer #(.enable("false")) multiplexer_2 (.in0(or_6_out), .in1(LED_EN), .out(multiplexer_2_out), .sel(LED_EN));
  or or_1 (or_1_out, and_2_out, and_12_out);
  or or_2 (or_2_out, and_9_out, and_22_out);
  or or_3 (or_3_out, and_7_out, LED_EN);
  and and_1 (and_1_out, comparator_1_eq, comparator_2_lt);
  or or_4 (or_4_out, START, and_8_out);
  Hex_Digit_Display hex_digit_display_1 (.value(HH_H));  // open: dp
  CNTR4U cntr4u_1 (
    .CLK(CLK), .LD(multiplexer_1_out), .CLR(or_1_out), .Q0(SS_L[0]), .Q1(SS_L[1]), .D0(SS0[0]), .D1(SS0[1]),
    .D2(SS0[2]), .Q2(SS_L[2]), .Q3(SS_L[3]), .D3(SS0[3]), .ENP(1'b1), .ENT(1'b1), .RCO(cntr4u_1_rco));
  CNTR4U cntr4u_2 (
    .CLK(CLK), .LD(multiplexer_1_out), .CLR(or_2_out), .Q0(MM_L[0]), .Q1(MM_L[1]), .D0(MM0[0]), .D1(MM0[1]),
    .D2(MM0[2]), .Q2(MM_L[2]), .Q3(MM_L[3]), .D3(MM0[3]), .ENP(and_12_out), .ENT(and_12_out),
    .RCO(cntr4u_2_rco));
  CNTR4U cntr4u_3 (
    .CLK(CLK), .LD(multiplexer_1_out), .CLR(or_3_out), .Q0(HH_L[0]), .Q1(HH_L[1]), .D0(HH0[0]), .D1(HH0[1]),
    .D2(HH0[2]), .Q2(HH_L[2]), .Q3(HH_L[3]), .D3(HH0[3]), .ENP(and_22_out), .ENT(and_22_out),
    .RCO(cntr4u_3_rco));
  or or_5 (or_5_out, comparator_1_lt, and_1_out);
  // CNTR4U cntr4u_4: pin names not known; wires that end beside it: CLK, STOP, or_4_out, 1'b1, 1'b0, 1'b0, 1'b0, multiplexer_2_out, multiplexer_2_out, cntr4u_4_p10, cntr4u_4_p10, cntr4u_4_p12[0], cntr4u_4_p12[1], cntr4u_4_p12[2], cntr4u_4_p12[3]
  Hex_Digit_Display hex_digit_display_2 (.value(HH_L), .dp(1'b1));
  Hex_Digit_Display hex_digit_display_3 (.value(MM_H));  // open: dp
  and and_2 (and_2_out, SS_L[0], SS_L[3]);
  not not_1 (not_1_out, SS_L[0]);
  and and_3 (and_3_out, SS_L[0], SS_L[3]);
  and and_4 (and_4_out, SS_L[3], not_1_out);
  and and_5 (and_5_out, MM_L[0], MM_L[3]);
  and and_6 (and_6_out, MM_L[3], MM_L[0]);
  and and_7 (and_7_out, HH_L[0], HH_L[3]);
  Comparator #(.width(4), .mode("unsigned")) comparator_5 (.a(HH1), .b(4'b1010), .lt(comparator_5_lt));  // open: gt, eq
  Comparator #(.width(4), .mode("unsigned")) comparator_6 (.a(HH0), .b(4'b1010), .lt(comparator_6_lt));  // open: gt, eq
  Comparator #(.width(4), .mode("unsigned")) comparator_7 (.a(MM1), .b(4'b1010), .lt(comparator_7_lt));  // open: gt, eq
  Comparator #(.width(4), .mode("unsigned")) comparator_8 (.a(MM0), .b(4'b1010), .lt(comparator_8_lt));  // open: gt, eq
  Comparator #(.width(4), .mode("unsigned")) comparator_9 (.a(SS1), .b(4'b1010), .lt(comparator_9_lt));  // open: gt, eq
  Comparator #(.width(4), .mode("unsigned")) comparator_10 (
    .a(SS0), .b(4'b1010), .lt(comparator_10_lt));  // open: gt, eq
  or or_6 (or_6_out, cntr4u_4_p12[3], cntr4u_4_p12[0], cntr4u_4_p12[2], cntr4u_4_p12[1]);
  and and_8 (and_8_out, cntr4u_4_p12[3], cntr4u_4_p12[1]);
  xor xor_1 (xor_1_out, cntr4u_4_p12[3], cntr4u_4_p12[2]);
  Decoder #(.select(4), .enable("false")) decoder_1 (
    .out0(decoder_1_out0), .out1(decoder_1_out1), .out2(decoder_1_out2), .out3(decoder_1_out3),
    .out4(decoder_1_out4), .out5(decoder_1_out5), .out6(decoder_1_out6), .out7(decoder_1_out7),
    .out8(decoder_1_out8), .out9(decoder_1_out9), .out10(decoder_1_out10), .out11(decoder_1_out11),
    .out12(decoder_1_out12), .out13(decoder_1_out13), .out14(decoder_1_out14), .out15(decoder_1_out15),
    .sel(cntr4u_4_p12));
  Hex_Digit_Display hex_digit_display_4 (.value(MM_L), .dp(1'b1));
  Hex_Digit_Display hex_digit_display_5 (.value(SS_H));  // open: dp
  CNTR4U cntr4u_5 (
    .CLK(CLK), .LD(multiplexer_1_out), .CLR(and_12_out), .Q0(SS_H[0]), .Q1(SS_H[1]), .D0(SS1[0]),
    .D1(SS1[1]), .D2(SS1[2]), .Q2(SS_H[2]), .Q3(SS_H[3]), .D3(SS1[3]), .ENP(and_2_out), .ENT(and_2_out),
    .RCO(cntr4u_5_rco));
  CNTR4U cntr4u_6 (
    .CLK(CLK), .LD(multiplexer_1_out), .CLR(and_22_out), .Q0(MM_H[0]), .Q1(MM_H[1]), .D0(MM1[0]),
    .D1(MM1[1]), .D2(MM1[2]), .Q2(MM_H[2]), .Q3(MM_H[3]), .D3(MM1[3]), .ENP(and_9_out), .ENT(and_9_out),
    .RCO(cntr4u_6_rco));
  and and_9 (and_9_out, and_18_out, and_5_out);
  CNTR4U cntr4u_7 (
    .CLK(CLK), .LD(multiplexer_1_out), .CLR(LED_EN), .Q0(HH_H[0]), .Q1(HH_H[1]), .D0(HH1[0]), .D1(HH1[1]),
    .D2(HH1[2]), .Q2(HH_H[2]), .Q3(HH_H[3]), .D3(HH1[3]), .ENP(and_7_out), .ENT(and_7_out), .RCO(cntr4u_7_rco));
  and and_10 (and_10_out, or_5_out, comparator_3_lt);
  and and_11 (and_11_out, comparator_5_lt, comparator_6_lt, comparator_7_lt, comparator_8_lt, comparator_9_lt, comparator_10_lt);
  xor xor_2 (xor_2_out, cntr4u_4_p12[2], cntr4u_4_p12[1]);
  xor xor_3 (xor_3_out, cntr4u_4_p12[1], cntr4u_4_p12[0]);
  // NOT_Gate not_2 has open pins: in=cntr4u_4_p12[3], out=open
  assign LED_R = or_8_out ? xor_3_out : 1'bz;  // Controlled_Buffer controlled_buffer_1
  assign LED_G = or_8_out ? xor_2_out : 1'bz;  // Controlled_Buffer controlled_buffer_2
  assign LED_B = or_8_out ? xor_1_out : 1'bz;  // Controlled_Buffer controlled_buffer_3
  xor xor_4 (xor_4_out, cntr4u_4_p12[2], cntr4u_4_p12[1]);
  or or_7 (or_7_out, xor_4_out, cntr4u_4_p12[0]);
  assign LED_R = or_9_out ? or_7_out : 1'bz;  // Controlled_Buffer controlled_buffer_4
  assign LED_G = or_9_out ? xor_4_out : 1'bz;  // Controlled_Buffer controlled_buffer_5
  assign LED_B = or_9_out ? cntr4u_4_p12[2] : 1'bz;  // Controlled_Buffer controlled_buffer_6
  Hex_Digit_Display hex_digit_display_6 (.value(SS_L), .dp(1'b1));
  and and_12 (and_12_out, SS_H[2], and_2_out, SS_H[0]);
  and and_13 (and_13_out, SS_H[0], SS_H[2]);
  and and_14 (and_14_out, MM_H[2], and_9_out, MM_H[0]);
  and and_15 (and_15_out, MM_H[0], MM_H[2]);
  and and_16 (and_16_out, HH_H[1], HH_L[0], HH_L[1]);
  and and_17 (and_17_out, and_10_out, comparator_4_lt, and_11_out);
  or or_8 (or_8_out, decoder_1_out0, decoder_1_out1, decoder_1_out2, decoder_1_out3, decoder_1_out5, decoder_1_out6, decoder_1_out7, decoder_1_out4);
  or or_9 (or_9_out, decoder_1_out8, decoder_1_out9, decoder_1_out15, decoder_1_out11, decoder_1_out12, decoder_1_out13, decoder_1_out14);
  and and_18 (and_18_out, and_12_out, SS_L[3], SS_L[0]);
  and and_19 (and_19_out, and_13_out, and_3_out);
  and and_20 (and_20_out, and_13_out, and_4_out);
  and and_21 (and_21_out, and_14_out, MM_L[3], MM_L[0]);
  not not_3 (not_3_out, and_17_out);
  assign LED_R = decoder_1_out10 ? 1'b1 : 1'bz;  // Controlled_Buffer controlled_buffer_7
  assign LED_G = decoder_1_out10 ? 1'b1 : 1'bz;  // Controlled_Buffer controlled_buffer_8
  assign LED_B = decoder_1_out10 ? 1'b0 : 1'bz;  // Controlled_Buffer controlled_buffer_9
  and and_22 (and_22_out, and_18_out, and_21_out);
  and and_23 (LED_EN, and_22_out, and_16_out);
  and and_24 (INErr, not_3_out, LD);
  // RGBLed RGBLED: pin names not known; wires that end beside it: cntr4u_5_rco, LED_R, LED_G, LED_B, RGBLED_p5
  and and_25 (and_25_out, and_15_out, and_6_out);
  and and_26 (STOP, and_19_out, and_25_out);
  and and_27 (START, and_25_out, and_20_out);

  // Other names for the same wires on the sheet: H0[3:0] = HH_L; H1[3:0] = HH_H; M0[3:0] = MM_L; M1[3:0] = MM_H;
  //   S0[3:0] = SS_L; S1[3:0] = SS_H

  // Notes on the sheet:
  //   设置初始时间BCD码
  //   输入信号
  //   请勿修改引脚名称、电路名称及电路封装外观
  //   数字时钟
  //   提示：使用4位二进制加法计数器子电路、比较器和独立逻辑门组件实现数字时钟。
  //   在载入有效时，检测设置数据错误
  //   生成三色LED显示信号，持续10个时钟周期
  //   59m
  //   59 58
  //   59 59
endmodule
